# Fritzing sketch MCUandMoistSensor (saved by Fritzing 0.9.4)

parts:
  U1 = NodeMCU V3.0
  Onderdeel1 = FC-28 Soil Hygrometer Module - Probe
  Onderdeel2 = FC-28 Soil Hygrometer Module

nets:
  N1: U1.D1, Onderdeel2.DO
  GND: U1.GND, Onderdeel2.GND
  3V3: U1.3V3, Onderdeel2.VCC
  N2: U1.A0, Onderdeel2.AO
  N3: Onderdeel1.POS, Onderdeel2.POS
  N4: Onderdeel1.NEG, Onderdeel2.NEG

custom parts:
  NodeMCU V3.0: ESP8266 based NodeMCU
  FC-28 Soil Hygrometer Module - Probe: The FC-28 is a soil hygrometer module that uses the Texas Instruments LM393 comparator chip to provide an analog measurement of soil humidity.
  FC-28 Soil Hygrometer Module: The FC-28 is a soil hygrometer module that uses the Texas Instruments LM393 comparator chip to provide an analog measurement of soil humidity. The digital output is high when soil moisture is over a certain threshold, as determined by adjusting the potentiometer.
