# Fritzing sketch MCUandMoistSensorMatrix (saved by Fritzing 0.9.4)

parts:
  U1 = NodeMCU V3.0
  Onderdeel1 = FC-28 Soil Hygrometer Module - Probe
  Onderdeel2 = FC-28 Soil Hygrometer Module
  8x8_LED_Modul_mit_MAX1 = 8x8 LED Modul mit MAX7219 [package=THT]

nets:
  N1: U1.D1, Onderdeel2.DO
  3V3: U1.3V3, Onderdeel2.VCC, 8x8_LED_Modul_mit_MAX1.VCC_Eingang
  GND: U1.GND, Onderdeel2.GND, 8x8_LED_Modul_mit_MAX1.GND_Eingang
  N2: U1.D5, 8x8_LED_Modul_mit_MAX1.CLK_Eingang
  N3: U1.D7, 8x8_LED_Modul_mit_MAX1.DIN_Eingang
  N4: U1.D8, 8x8_LED_Modul_mit_MAX1.CS_Eingang
  N5: U1.A0, Onderdeel2.AO
  N6: Onderdeel1.POS, Onderdeel2.NEG
  N7: Onderdeel1.NEG, Onderdeel2.POS

custom parts:
  NodeMCU V3.0: ESP8266 based NodeMCU
  FC-28 Soil Hygrometer Module - Probe: The FC-28 is a soil hygrometer module that uses the Texas Instruments LM393 comparator chip to provide an analog measurement of soil humidity.
  FC-28 Soil Hygrometer Module: The FC-28 is a soil hygrometer module that uses the Texas Instruments LM393 comparator chip to provide an analog measurement of soil humidity. The digital output is high when soil moisture is over a certain threshold, as determined by adjusting the potentiometer.
